# Fritzing sketch Sema spajanja (saved by Fritzing 1.0.5)
breadboards: 1

parts:
  Mod1 = Raspberry Pi Pico
  S1 = Pushbutton [package="[THT]"]
  S2 = Pushbutton [package="[THT]"]
  Keypad4x1 = Keypad Membran 4x4
  TFT1 = Color 320x240 TFT Display, ILI9341 Controller Chip
  Mod2 = Passive Buzzer
  PIR1 = PIR sensor

nets:
  N1: Mod1.pin_1, Keypad4x1.Pin5
  N2: Mod1.pin_2, Keypad4x1.Pin6
  GND: Mod1.pin_3, Mod1.pin_23, Mod1.pin_33, Mod1.pin_38, TFT1.GND, Mod2.-, PIR1.GND
  N3: Mod1.pin_4, Keypad4x1.Pin7
  N4: Mod1.pin_5, Keypad4x1.Pin8
  N5: Mod1.pin_10, PIR1.SIG
  N6: Mod1.pin_14, S1.Pin_3, S1.Pin_4
  N7: Mod1.pin_17, S2.Pin_3, S2.Pin_4
  N8: Mod1.pin_20, TFT1.D/C
  N9: Mod1.pin_21, TFT1.MISO
  N10: Mod1.pin_22, TFT1.CS
  N11: Mod1.pin_24, TFT1.SCK
  N12: Mod1.pin_25, TFT1.MOSI
  N13: Mod1.pin_26, TFT1.Reset
  N14: Mod1.pin_27, Keypad4x1.Pin1
  N15: Mod1.pin_29, Keypad4x1.Pin2
  N16: Mod1.pin_31, Keypad4x1.Pin3
  N17: Mod1.pin_32, Keypad4x1.Pin4
  N18: Mod1.pin_34, Mod2.NC
  VCC: Mod1.pin_36, S1.Pin_1, S1.Pin_2, S2.Pin_1, S2.Pin_2, TFT1.VCC, Mod2.S, PIR1.VDD

notes:
  Za tastere koristimo interni PULL_DOWN otpornik u programskom kodu
  Senzor pokreta
  Buzzer - PWM izlaz

custom parts:
  Raspberry Pi Pico: Raspberry Pi Pico. Based around the RP2040 microcontroller the Pico is a low cost microcontroller device bringing Raspberry Pi quality, cost, and easy of use to the microcontroller space. Jan 2021, Split part in to two versions: tht (this one) and SMD. This one will drill holes for a .1 in header in pcb to allow plugging in the module as well as providing pads to solder the module to the top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
  Keypad Membran 4x4: Membrane Keypad 4x4 Matrix
  Color 320x240 TFT Display, ILI9341 Controller Chip: 2.2" TFT Display with ILI9341 Controller
